// Logisim project Ejercicio3.circ as structural Verilog: 1 circuit, main circuit main
module main (
  input  A1,
  input  A2,
  input  in_3,
  input  B1,
  input  B2,
  input  B3,
  output out_7
);

  wire and_1_out, and_2_out, and_3_out, and_4_out, and_5_out, and_6_out, and_7_out, and_8_out, and_9_out,
       and_10_out, and_11_out, and_12_out, not_1_out, not_2_out, not_3_out, not_4_out, not_5_out, not_6_out,
       not_7_out, not_8_out, not_9_out, not_10_out, not_11_out, not_12_out, not_13_out, not_14_out,
       not_15_out, not_16_out, not_17_out, not_18_out, not_19_out, not_20_out, not_21_out, not_22_out,
       not_23_out, not_24_out;

  not not_1 (not_1_out, A1);
  not not_2 (not_2_out, B1);
  not not_3 (not_3_out, A2);
  not not_4 (not_4_out, B2);
  not not_5 (not_5_out, in_3);
  not not_6 (not_6_out, B3);
  not not_7 (not_7_out, A1);
  and and_1 (and_1_out, not_1_out, not_2_out);
  not not_8 (not_8_out, B1);
  not not_9 (not_9_out, A2);
  and and_2 (and_2_out, not_3_out, not_4_out);
  not not_10 (not_10_out, B2);
  not not_11 (not_11_out, in_3);
  and and_3 (and_3_out, not_5_out, not_6_out);
  not not_12 (not_12_out, B3);
  and and_4 (and_4_out, not_7_out, not_13_out);
  not not_13 (not_13_out, and_1_out);
  not not_14 (not_14_out, and_1_out);
  and and_5 (and_5_out, not_14_out, not_8_out);
  and and_6 (and_6_out, not_9_out, not_15_out);
  not not_15 (not_15_out, and_2_out);
  not not_16 (not_16_out, and_2_out);
  and and_7 (and_7_out, not_16_out, not_10_out);
  and and_8 (and_8_out, not_11_out, not_17_out);
  not not_17 (not_17_out, and_3_out);
  not not_18 (not_18_out, and_3_out);
  and and_9 (and_9_out, not_18_out, not_12_out);
  not not_19 (not_19_out, and_4_out);
  not not_20 (not_20_out, and_5_out);
  not not_21 (not_21_out, and_6_out);
  not not_22 (not_22_out, and_7_out);
  not not_23 (not_23_out, and_8_out);
  not not_24 (not_24_out, and_9_out);
  and and_10 (and_10_out, not_19_out, not_20_out);
  and and_11 (and_11_out, not_21_out, not_22_out);
  and and_12 (and_12_out, not_23_out, not_24_out);
  and and_13 (out_7, and_10_out, and_11_out, and_12_out);

  // Notes on the sheet:
  //   A3
endmodule
