// Logisim project Ejercicio1.circ as structural Verilog: 1 circuit, main circuit Multiplexor
module Multiplexor (
  input  in_1,
  input  in_2,
  input  in_3,
  input  in_4,
  input  in_5,
  input  in_6,
  input  in_7,
  input  in_8,
  input  A,
  input  B,
  input  C,
  output out_12
);

  wire and_1_out, and_2_out, and_3_out, and_4_out, and_5_out, and_6_out, and_7_out, and_8_out, not_1_out,
       not_2_out, not_3_out;

  not not_1 (not_1_out, A);
  not not_2 (not_2_out, C);
  not not_3 (not_3_out, B);
  and and_1 (and_1_out, not_2_out, not_3_out, not_1_out, in_1);
  and and_2 (and_2_out, in_2, not_1_out, not_3_out, C);
  and and_3 (and_3_out, in_3, not_1_out, B, not_2_out);
  and and_4 (and_4_out, in_4, not_1_out, B, C);
  and and_5 (and_5_out, in_5, A, not_3_out, not_2_out);
  and and_6 (and_6_out, in_6, A, not_3_out, C);
  and and_7 (and_7_out, in_7, A, B, not_2_out);
  and and_8 (and_8_out, in_8, A, B, C);
  or or_1 (out_12, and_1_out, and_2_out, and_3_out, and_4_out, and_5_out, and_6_out, and_7_out, and_8_out);
endmodule
