// Logisim project flipFlopT.circ as structural Verilog: 1 circuit, main circuit main
module main (
  input  Entrada_usuario,
  input  in_2,
  input  in_3,
  input  in_4,
  input  Cadena_a_aceptar,
  input  in_6,
  input  in_7,
  input  in_8,
  input  T,
  input  in_10,
  input  in_11,
  input  in_12,
  input  in_13,
  output out_14,
  output out_15,
  output out_16
);

  wire and_1_out, and_2_out, and_3_out, and_4_out, and_5_out, and_6_out, and_7_out, and_8_out, and_9_out,
       and_10_out, and_11_out, and_12_out, and_13_out, and_14_out, and_15_out, and_16_out, and_17_out,
       j_k_ff_1_q, not_1_out, not_2_out, not_3_out, not_4_out, not_5_out, not_6_out, not_7_out, not_8_out,
       not_9_out, not_10_out, not_11_out, not_12_out, not_13_out, not_14_out, not_15_out, not_16_out,
       not_17_out, not_18_out, not_19_out, not_20_out, not_21_out, not_22_out, not_23_out, not_24_out,
       not_25_out, not_26_out, not_27_out, not_28_out, not_29_out, not_30_out, not_31_out, not_32_out;

  not not_1 (not_1_out, Entrada_usuario);
  not not_2 (not_2_out, Entrada_usuario);
  and and_1 (and_1_out, not_2_out, not_3_out);
  not not_3 (not_3_out, Cadena_a_aceptar);
  not not_4 (not_4_out, Cadena_a_aceptar);
  not not_5 (not_5_out, in_2);
  not not_6 (not_6_out, in_2);
  and and_2 (and_2_out, not_6_out, not_7_out);
  not not_7 (not_7_out, in_6);
  not not_8 (not_8_out, in_6);
  not not_9 (not_9_out, in_3);
  not not_10 (not_10_out, in_3);
  and and_3 (and_3_out, not_10_out, not_11_out);
  not not_11 (not_11_out, in_7);
  not not_12 (not_12_out, in_7);
  not not_13 (not_13_out, in_4);
  not not_14 (not_14_out, in_4);
  and and_4 (and_4_out, not_14_out, not_15_out);
  not not_15 (not_15_out, in_8);
  not not_16 (not_16_out, in_8);
  not not_17 (not_17_out, and_1_out);
  not not_18 (not_18_out, and_1_out);
  not not_19 (not_19_out, and_2_out);
  not not_20 (not_20_out, and_2_out);
  not not_21 (not_21_out, and_3_out);
  not not_22 (not_22_out, and_3_out);
  not not_23 (not_23_out, and_4_out);
  not not_24 (not_24_out, and_4_out);
  and and_5 (and_5_out, not_1_out, not_17_out);
  and and_6 (and_6_out, not_18_out, not_4_out);
  and and_7 (and_7_out, not_5_out, not_19_out);
  and and_8 (and_8_out, not_20_out, not_8_out);
  and and_9 (and_9_out, not_9_out, not_21_out);
  and and_10 (and_10_out, not_22_out, not_12_out);
  and and_11 (and_11_out, not_13_out, not_23_out);
  and and_12 (and_12_out, not_24_out, not_16_out);
  not not_25 (not_25_out, and_5_out);
  not not_26 (not_26_out, and_6_out);
  not not_27 (not_27_out, and_7_out);
  not not_28 (not_28_out, and_8_out);
  not not_29 (not_29_out, and_9_out);
  not not_30 (not_30_out, and_10_out);
  not not_31 (not_31_out, and_11_out);
  not not_32 (not_32_out, and_12_out);
  and and_13 (and_13_out, not_25_out, not_26_out);
  and and_14 (and_14_out, not_27_out, not_28_out);
  and and_15 (and_15_out, not_29_out, not_30_out);
  and and_16 (and_16_out, not_31_out, not_32_out);
  and and_17 (and_17_out, and_13_out, and_14_out, and_15_out, and_16_out);
  J_K_Flip_Flop j_k_ff_1 (.J(in_12), .clk(and_17_out), .K(in_12), .Q(j_k_ff_1_q));  // open: Qn, preset, en, reset
  J_K_Flip_Flop j_k_ff_2 (.J(T), .clk(in_10), .K(in_11), .Q(out_14), .Qn(out_15));  // open: preset, en, reset
  J_K_Flip_Flop j_k_ff_3 (.J(in_13), .clk(j_k_ff_1_q), .K(in_13), .Q(out_16));  // open: Qn, preset, en, reset

  // Notes on the sheet:
  //   Compara las entradas, devuelve 1 si son iguales
  //   * Flip Flop T de la forma, se forma con un JK
  //   Al tercer estado incorrecto debe cambiar a 1
  //   Ambos valores auxiliares asi como el Flip FLop deben valer 1
  //   Aunque el programa siempre los restablezca a 0
  //   *
endmodule
